// Logisim project 1bitRegister.circ as structural Verilog: 1 circuit, main circuit 1 bit register
// 1-bit register
module _1_bit_register (
  input  clock,
  input  data,
  input  clear,
  input  load,
  output data_out
);

  wire and_1_out, and_2_out, not_1_out, not_2_out;

  and and_1 (and_1_out, data, load);
  not not_1 (not_1_out, data);
  and and_2 (and_2_out, not_1_out, load);
  J_K_Flip_Flop j_k_ff_1 (
    .J(and_1_out), .clk(clock), .K(and_2_out), .Q(data_out), .preset(1'b0), .en(not_2_out), .reset(clear));  // open: Qn
  not not_2 (not_2_out, clear);

  // Notes on the sheet:
  //   Isha Mudgal
  //   CLA 5
  //   1-bit register
endmodule
