// Logisim project RSC.circ as structural Verilog: 9 circuits, main circuit Arith_U
// AU
module Arith_U (
  input  [31:0] A,
  input  [31:0] B,
  input  S1,
  input  S0,
  output [31:0] AU_out
);

  wire and_2_out, nor_1_out, or_1_out;
  wire [31:0] adder_1_out, and_1_out, multiplexer_1_out, not_1_out, not_2_out;

  assign not_1_out = ~B;  // NOT_Gate not_1, 32 bits wide
  assign and_1_out = A & not_2_out;  // AND_Gate and_1, 32 bits wide
  assign not_2_out = ~A;  // NOT_Gate not_2, 32 bits wide
  Multiplexer #(.select(2), .width(32), .enable("false")) multiplexer_1 (
    .in0(not_1_out), .in1(B), .in2(and_1_out), .out(multiplexer_1_out), .sel({S1, S0}));  // open: in3
  Adder #(.width(32)) adder_1 (.a(A), .b(multiplexer_1_out), .out(adder_1_out), .cin(or_1_out));  // open: cout
  nor nor_1 (nor_1_out, S1, S0);
  or or_1 (or_1_out, S1, nor_1_out);
  Multiplexer #(.width(32), .enable("false")) multiplexer_2 (.in0(adder_1_out), .in1(B), .out(AU_out), .sel(and_2_out));
  and and_2 (and_2_out, S1, S0);

  // Notes on the sheet:
  //   Isha Mudgal
  //   CLA4
  //   AU
endmodule

// LU
module Logic_U (
  input  [31:0] A,
  input  [31:0] B,
  input  S1,
  input  S0,
  output [31:0] Logic_Out
);

  wire [31:0] and_1_out, not_1_out, or_1_out, shifter_1_out;

  assign and_1_out = A & B;  // AND_Gate and_1, 32 bits wide
  assign or_1_out = A | B;  // OR_Gate or_1, 32 bits wide
  assign not_1_out = ~A;  // NOT_Gate not_1, 32 bits wide
  Shifter #(.width(32), .shift("ar")) shifter_1 (.in(A), .\dist (5'b00001), .out(shifter_1_out));
  Multiplexer #(.select(2), .width(32), .enable("false")) multiplexer_1 (
    .in0(and_1_out), .in1(or_1_out), .in2(shifter_1_out), .in3(not_1_out), .out(Logic_Out), .sel({S1, S0}));

  // Notes on the sheet:
  //   Isha Mudgal
  //   CLA 6
  //   Logic Unit
endmodule

module ALU (
  input  [31:0] A,
  input  [31:0] B,
  input  S2,
  input  S1,
  input  S0,
  output [31:0] ALU_out
);

  wire [31:0] arith_u_1_au_out, logic_u_1_logic_out;

  Arith_U arith_u_1 (.A(A), .B(B), .S1(S1), .S0(S0), .AU_out(arith_u_1_au_out));
  Logic_U logic_u_1 (.A(A), .B(B), .S1(S1), .S0(S0), .Logic_Out(logic_u_1_logic_out));
  Multiplexer #(.width(32), .enable("false")) multiplexer_1 (
    .in0(arith_u_1_au_out), .in1(logic_u_1_logic_out), .out(ALU_out), .sel(S2));

  // Notes on the sheet:
  //   Isha Mudgal
  //   CLA 6
  //   Logic Unit
endmodule

module SC (
  input  Clock,
  input  Clear,
  output [2:0] SEQ_Out
);

  wire not_1_out;
  wire [2:0] adder_1_out;

  Adder #(.width(3)) adder_1 (.a(3'b001), .b(SEQ_Out), .out(adder_1_out));  // open: cin, cout
  not not_1 (not_1_out, Clear);
  Register #(.width(3)) register_1 (.D(adder_1_out), .en(not_1_out), .Q(SEQ_Out), .clk(Clock), .clr(Clear));

  // Notes on the sheet:
  //   Isha Mudgal
  //   cla7
  //   SC
endmodule

module RSC (
);

  wire AR_LD, control_1_acc_bus, control_1_acc_clr, control_1_acc_ld, control_1_dr_bus, control_1_dr_ld,
       control_1_ir_ld, control_1_outr_ld, control_1_pc_bus, control_1_pc_ld, control_1_r_bus,
       control_1_r_ld, control_1_ram_en, control_1_ram_r_prime_w, control_1_z_ld, PC_IN, Primary_Clock_out,
       z_reg_1_z_out;
  wire [2:0] control_1_alu_s;
  wire [3:0] outr_1_data_out, outr_1_data_out_2, outr_1_data_out_3, outr_1_data_out_4, outr_1_data_out_5,
       outr_1_data_out_6, outr_1_data_out_7, outr_1_data_out_8;
  wire [31:0] acc_1_out_6, alu_1_alu_out, ar_1_data_out, dr_1_data_out, ir_1_data_out, r_1_bus_out;

  Clock Primary_Clock (.out(Primary_Clock_out));
  Hex_Digit_Display hex_digit_display_1 (.value(outr_1_data_out_8));  // open: dp
  AR ar_1 (.data_IN(r_1_bus_out), .Clock(Primary_Clock_out), .Load(AR_LD), .data_OUT(ar_1_data_out));
  R r_1 (
    .data_IN(r_1_bus_out), .Load(control_1_r_ld), .Clock(Primary_Clock_out), .Bus(control_1_r_bus),
    .bus_OUT(r_1_bus_out));  // open: data_OUT
  ALU alu_1 (
    .A(acc_1_out_6), .B(r_1_bus_out), .S2(control_1_alu_s[2]), .S1(control_1_alu_s[1]),
    .S0(control_1_alu_s[0]), .ALU_out(alu_1_alu_out));
  Hex_Digit_Display hex_digit_display_2 (.value(outr_1_data_out_7));  // open: dp
  Hex_Digit_Display hex_digit_display_3 (.value(outr_1_data_out_6));  // open: dp
  Hex_Digit_Display hex_digit_display_4 (.value(outr_1_data_out_5));  // open: dp
  DR dr_1 (
    .data_IN(r_1_bus_out), .Load(control_1_dr_ld), .Clock(Primary_Clock_out), .Bus(control_1_dr_bus),
    .data_OUT(dr_1_data_out), .bus_OUT(r_1_bus_out));
  ACC acc_1 (
    .Data_IN(alu_1_alu_out), .Load(control_1_acc_ld), .Clock(Primary_Clock_out), .Clear(control_1_acc_clr),
    .Bus(control_1_acc_bus), .out_6(acc_1_out_6), .out_7(r_1_bus_out));
  Hex_Digit_Display hex_digit_display_5 (.value(outr_1_data_out_4));  // open: dp
  RAM #(.addrWidth(16), .dataWidth(32)) ram_1 (
    .addr(ar_1_data_out[15:0]), .data(r_1_bus_out), .sel(control_1_ram_en), .clk(Primary_Clock_out),
    .ld(control_1_ram_r_prime_w), .clr(1'b0));
  PC pc_1 (
    .data_IN(r_1_bus_out), .Count(PC_IN), .Load(control_1_pc_ld), .Clock(Primary_Clock_out),
    .Bus(control_1_pc_bus), .out_7(r_1_bus_out));  // open: out_6
  OUTR outr_1 (
    .data_IN(r_1_bus_out), .Clock(Primary_Clock_out), .Load(control_1_outr_ld),
    .data_OUT({outr_1_data_out_8, outr_1_data_out_7, outr_1_data_out_6, outr_1_data_out_5, outr_1_data_out_4, outr_1_data_out_3, outr_1_data_out_2, outr_1_data_out}));
  Hex_Digit_Display hex_digit_display_6 (.value(outr_1_data_out_3));  // open: dp
  IR ir_1 (.data_IN(dr_1_data_out), .Clock(Primary_Clock_out), .Load(control_1_ir_ld), .data_OUT(ir_1_data_out));
  Z_Reg z_reg_1 (.ACC_in(acc_1_out_6), .Clock(Primary_Clock_out), .Load(control_1_z_ld), .Z_out(z_reg_1_z_out));
  Hex_Digit_Display hex_digit_display_7 (.value(outr_1_data_out));  // open: dp
  Hex_Digit_Display hex_digit_display_8 (.value(outr_1_data_out_2));  // open: dp
  Control control_1 (
    .RAM_R_prime_W(control_1_ram_r_prime_w), .RAM_EN(control_1_ram_en), .AR_LD(AR_LD),
    .PC_BUS(control_1_pc_bus), .PC_INC(PC_IN), .PC_LD(control_1_pc_ld), .DR_BUS(control_1_dr_bus),
    .DR_LD(control_1_dr_ld), .R_BUS(control_1_r_bus), .R_LD(control_1_r_ld), .ACC_BUS(control_1_acc_bus),
    .ACC_CLR(control_1_acc_clr), .ACC_LD(control_1_acc_ld), .ALU_S(control_1_alu_s),
    .OUTR_LD(control_1_outr_ld), .Z_LD(control_1_z_ld), .IR_LD(control_1_ir_ld), .clock(Primary_Clock_out),
    .Z_in(z_reg_1_z_out), .IR_in(ir_1_data_out));  // open: T, D

  // Notes on the sheet:
  //   Isha Mudgal
  //   OLA 7
  //   RSC
endmodule

module Decoder (
  input  [31:0] IR_In,
  output [15:0] D_out,
  output [3:0] Debug_INSTRUCTION
);

  wire or_1_out;
  wire [3:0] or_2_out;
  wire [15:0] decoder_1_out0;

  Multiplexer #(.width(16), .enable("false")) multiplexer_1 (
    .in0(decoder_1_out0), .in1({16{1'b0}}), .out(D_out), .sel(or_1_out));
  or or_1 (or_1_out, or_2_out[0], or_2_out[1], or_2_out[2], or_2_out[3]);
  assign or_2_out = IR_In[7:4] | IR_In[11:8] | IR_In[15:12] | IR_In[19:16] | IR_In[23:20] | IR_In[27:24] | IR_In[31:28];  // OR_Gate or_2, 4 bits wide
  Decoder_part #(.select(4), .enable("false")) decoder_1 (
    .out0(decoder_1_out0[0]), .out1(decoder_1_out0[1]), .out2(decoder_1_out0[2]), .out3(decoder_1_out0[3]),
    .out4(decoder_1_out0[4]), .out5(decoder_1_out0[5]), .out6(decoder_1_out0[6]), .out7(decoder_1_out0[7]),
    .out8(decoder_1_out0[8]), .out9(decoder_1_out0[9]), .out10(decoder_1_out0[10]),
    .out11(decoder_1_out0[11]), .out12(decoder_1_out0[12]), .out13(decoder_1_out0[13]),
    .out14(decoder_1_out0[14]), .out15(decoder_1_out0[15]), .sel(IR_In[3:0]));

  assign Debug_INSTRUCTION = IR_In[3:0];

  // Notes on the sheet:
  //   Isha Mudgal
  //   CLA 8
  //   Decoder
endmodule

module Timer (
  input  Clear,
  input  Clock,
  input  Stop,
  output [7:0] T_out
);

  wire [2:0] sc_1_seq_out;
  wire [7:0] decoder_1_out0;

  Multiplexer #(.width(8), .enable("false")) multiplexer_1 (
    .in0(decoder_1_out0), .in1({8{1'b0}}), .out(T_out), .sel(Stop));
  Decoder_part #(.select(3), .enable("false")) decoder_1 (
    .out0(decoder_1_out0[0]), .out1(decoder_1_out0[1]), .out2(decoder_1_out0[2]), .out3(decoder_1_out0[3]),
    .out4(decoder_1_out0[4]), .out5(decoder_1_out0[5]), .out6(decoder_1_out0[6]), .out7(decoder_1_out0[7]),
    .sel(sc_1_seq_out));
  SC sc_1 (.Clock(Clock), .Clear(Clear), .SEQ_Out(sc_1_seq_out));

  // Notes on the sheet:
  //   Isha Mudgal
  //   CLA 8
  //   Timer
endmodule

// Z
module Z_Reg (
  input  Clock,
  input  [31:0] ACC_in,
  input  Load,
  output Z_out
);

  wire not_1_out, or_1_out;

  or or_1 (or_1_out, ACC_in[0], ACC_in[1], ACC_in[2], ACC_in[3], ACC_in[4], ACC_in[5], ACC_in[6], ACC_in[7], ACC_in[8], ACC_in[9], ACC_in[10], ACC_in[11], ACC_in[12], ACC_in[13], ACC_in[14], ACC_in[15], ACC_in[17], ACC_in[18], ACC_in[19], ACC_in[20], ACC_in[21], ACC_in[22], ACC_in[23], ACC_in[24], ACC_in[25], ACC_in[26], ACC_in[27], ACC_in[28], ACC_in[29], ACC_in[30], ACC_in[31], ACC_in[16]);
  not not_1 (not_1_out, or_1_out);
  _1_bit_register u_1_bit_register_1 (.data(not_1_out), .clock(Clock), .load(Load), .data_out(Z_out));  // open: clear

  // Notes on the sheet:
  //   Isha
  //   OLA 7
  //   Z Reg
endmodule

module Control (
  input  clock,
  input  [31:0] IR_in,
  input  Z_in,
  output IR_LD,
  output RAM_R_prime_W,
  output [7:0] T,
  output RAM_EN,
  output AR_LD,
  output PC_BUS,
  output [3:0] D,
  output PC_INC,
  output PC_LD,
  output DR_BUS,
  output DR_LD,
  output R_BUS,
  output R_LD,
  output ACC_BUS,
  output ACC_CLR,
  output ACC_LD,
  output [2:0] ALU_S,
  output OUTR_LD,
  output Z_LD
);

  wire S_data_out, s_ld_1_s_ld, sc_clr_1_sc_clr;
  wire [7:0] timer_1_t_out;
  wire [15:0] decoder_1_d_out;

  IR_LD ir_ld_1 (.t2(timer_1_t_out[2]), .clock(clock), .IR_LD(IR_LD));
  RAM_RW ram_rw_1 (
    .t1(timer_1_t_out[1]), .t3(timer_1_t_out[3]), .t5(timer_1_t_out[5]), .d1(decoder_1_d_out[1]),
    .d2(decoder_1_d_out[2]), .d5(decoder_1_d_out[5]), .d6(decoder_1_d_out[6]), .z(Z_in),
    .RAM_RW(RAM_R_prime_W));
  RAM_EN ram_en_1 (
    .t1(timer_1_t_out[1]), .t3(timer_1_t_out[3]), .t5(timer_1_t_out[5]), .t6(timer_1_t_out[6]),
    .d1(decoder_1_d_out[1]), .d2(decoder_1_d_out[2]), .d5(decoder_1_d_out[5]), .d6(decoder_1_d_out[6]),
    .z(Z_in), .RAM_EN(RAM_EN));
  AR_LD ar_ld_1 (
    .t0(timer_1_t_out[0]), .t2(timer_1_t_out[2]), .t4(timer_1_t_out[4]), .clock(clock),
    .d1(decoder_1_d_out[1]), .d2(decoder_1_d_out[2]), .AR_LD(AR_LD));
  PC_BUS pc_bus_1 (.t0(timer_1_t_out[0]), .t2(timer_1_t_out[2]), .PC_BUS(PC_BUS));
  PC_INC pc_inc_1 (
    .t1(timer_1_t_out[1]), .t3(timer_1_t_out[3]), .clock(clock), .d1(decoder_1_d_out[1]),
    .d2(decoder_1_d_out[2]), .d6(decoder_1_d_out[6]), .z(Z_in), .PC_INC(PC_INC));
  PC_LD pc_ld_1 (
    .t4(timer_1_t_out[4]), .clock(clock), .d5(decoder_1_d_out[5]), .d6(decoder_1_d_out[6]), .z(Z_in),
    .PC_LD(PC_LD));
  DR_BUS dr_bus_1 (
    .t4(timer_1_t_out[4]), .t6(timer_1_t_out[6]), .d1(decoder_1_d_out[1]), .d2(decoder_1_d_out[2]),
    .d5(decoder_1_d_out[5]), .d6(decoder_1_d_out[6]), .z(Z_in), .DR_BUS(DR_BUS));
  DR_LD dr_ld_1 (
    .t1(timer_1_t_out[1]), .t3(timer_1_t_out[3]), .t5(timer_1_t_out[5]), .clock(clock),
    .d1(decoder_1_d_out[1]), .d2(decoder_1_d_out[2]), .d5(decoder_1_d_out[5]), .d6(decoder_1_d_out[6]),
    .z(Z_in), .DR_LD(DR_LD));
  R_BUS r_bus_1 (
    .t3(timer_1_t_out[3]), .d4(decoder_1_d_out[4]), .d8(decoder_1_d_out[8]), .d9(decoder_1_d_out[9]),
    .d12(decoder_1_d_out[12]), .d13(decoder_1_d_out[13]), .R_BUS(R_BUS));
  R_LD r_ld_1 (.t3(timer_1_t_out[3]), .clock(clock), .d3(decoder_1_d_out[3]), .R_LD(R_LD));
  ACC_BUS acc_bus_1 (
    .t3(timer_1_t_out[3]), .t5(timer_1_t_out[5]), .d2(decoder_1_d_out[2]), .d3(decoder_1_d_out[3]),
    .d7(decoder_1_d_out[7]), .ACC_BUS(ACC_BUS));
  ACC_CLR acc_clr_1 (.t3(timer_1_t_out[3]), .d11(decoder_1_d_out[11]), .ACC_CLR(ACC_CLR));
  ACC_LD acc_ld_1 (
    .t3(timer_1_t_out[3]), .t6(timer_1_t_out[6]), .clock(clock), .d1(decoder_1_d_out[1]),
    .d4(decoder_1_d_out[4]), .d8(decoder_1_d_out[8]), .d9(decoder_1_d_out[9]), .d10(decoder_1_d_out[10]),
    .d12(decoder_1_d_out[12]), .d13(decoder_1_d_out[13]), .d14(decoder_1_d_out[14]),
    .d15(decoder_1_d_out[15]), .ACC_LD(ACC_LD));
  ALU_SEL alu_sel_1 (
    .d1(decoder_1_d_out[1]), .d4(decoder_1_d_out[4]), .d9(decoder_1_d_out[9]), .d10(decoder_1_d_out[10]),
    .d12(decoder_1_d_out[12]), .d13(decoder_1_d_out[13]), .d14(decoder_1_d_out[14]),
    .d15(decoder_1_d_out[15]), .s2(ALU_S[2]), .s1(ALU_S[1]), .s0(ALU_S[0]));
  OUTR_LD outr_ld_1 (.t3(timer_1_t_out[3]), .clock(clock), .d7(decoder_1_d_out[7]), .OUTR_LD(OUTR_LD));
  Z_LD z_ld_1 (.out_1(Z_LD));
  S_LD s_ld_1 (.t3(timer_1_t_out[3]), .clock(clock), .d0(decoder_1_d_out[0]), .S_LD(s_ld_1_s_ld));
  SC_CLR sc_clr_1 (
    .t4(timer_1_t_out[4]), .t5(timer_1_t_out[5]), .t7(timer_1_t_out[7]), .d1(decoder_1_d_out[1]),
    .d2(decoder_1_d_out[2]), .d5(decoder_1_d_out[5]), .d6(decoder_1_d_out[6]), .z(Z_in),
    .SC_CLR(sc_clr_1_sc_clr));
  Timer timer_1 (.T_out(timer_1_t_out), .Clear(sc_clr_1_sc_clr), .Clock(clock), .Stop(S_data_out));
  _1_bit_register S (.data(1'b1), .clock(clock), .load(s_ld_1_s_ld), .clear(1'b0), .data_out(S_data_out));
  Decoder decoder_1 (.D_out(decoder_1_d_out), .IR_In(IR_in));  // open: Debug_INSTRUCTION

  // Notes on the sheet:
  //   Isha Mudgal
  //   OLA 7
  //   Control
endmodule
