// Logisim project custom_reg.circ as structural Verilog: 11 circuits, main circuit Register
module Register (
  input  [31:0] Data_In,
  input  Clock,
  input  Load,
  output [31:0] Data_Out
);

  Register_part #(.width(32)) register_1 (.D(Data_In), .en(Load), .Q(Data_Out), .clk(Clock));  // open: clr

  // Notes on the sheet:
  //   Isha Mudgal
  //   OLA 5
  //   register
endmodule

module BusRegister (
  input  [31:0] Data_In,
  input  Load,
  input  Clock,
  input  Bus,
  output [31:0] Data_Out,
  output [31:0] Bus_Out
);

  Register_part #(.width(32)) register_1 (.D(Data_In), .en(Load), .Q(Data_Out), .clk(Clock));  // open: clr
  assign Bus_Out = Bus ? Data_Out : 32'bz;  // Controlled_Buffer controlled_buffer_1

  // Notes on the sheet:
  //   Isha Mudgal
  //   OLA 5
  //   Bus reg
endmodule

module ClearRegister (
  input  [31:0] Data_In,
  input  Load,
  input  Clock,
  input  Clear,
  input  Bus,
  output [31:0] Data_Out,
  output [31:0] Bus_Out
);

  Register_part #(.width(32)) register_1 (.D(Data_In), .en(Load), .Q(Data_Out), .clk(Clock), .clr(Clear));
  assign Bus_Out = Bus ? Data_Out : 32'bz;  // Controlled_Buffer controlled_buffer_1

  // Notes on the sheet:
  //   Isha Mudgal
  //   OLA 5
  //   Clear reg
endmodule

module CountRegister (
  input  [31:0] Data_In,
  input  Load,
  input  Clock,
  input  Bus,
  input  Count,
  output [31:0] Data_Out,
  output [31:0] Bus_Out
);

  wire or_1_out;
  wire [31:0] adder_1_out, multiplexer_1_out;

  Adder #(.width(32)) adder_1 (.a(32'h1), .b(Data_Out), .out(adder_1_out));  // open: cin, cout
  Multiplexer #(.width(32), .enable("false")) multiplexer_1 (
    .in0(Data_In), .in1(adder_1_out), .out(multiplexer_1_out), .sel(Count));
  or or_1 (or_1_out, Count, Load);
  Register_part #(.width(32)) register_1 (
    .D(multiplexer_1_out), .en(or_1_out), .Q(Data_Out), .clk(Clock));  // open: clr
  assign Bus_Out = Bus ? Data_Out : 32'bz;  // Controlled_Buffer controlled_buffer_1

  // Notes on the sheet:
  //   Isha Mudgal
  //   OLA 5
  //   Count reg
endmodule

module ACC (
  input  [31:0] Data_IN,
  input  Load,
  input  Clock,
  input  Clear,
  input  Bus,
  output [31:0] out_6,
  output [31:0] out_7
);

  ClearRegister clearregister_1 (
    .Data_In(Data_IN), .Load(Load), .Clock(Clock), .Clear(Clear), .Bus(Bus), .Data_Out(out_6), .Bus_Out(out_7));

  // Notes on the sheet:
  //   Isha Mudgal
  //   OLA 5
  //   ACC
endmodule

module AR (
  input  [31:0] data_IN,
  input  Clock,
  input  Load,
  output [31:0] data_OUT
);

  Register register_1 (.Data_In(data_IN), .Clock(Clock), .Load(Load), .Data_Out(data_OUT));

  // Notes on the sheet:
  //   Isha Mudgal
  //   OLA 5
  //   AR
endmodule

module DR (
  input  [31:0] data_IN,
  input  Load,
  input  Clock,
  input  Bus,
  output [31:0] data_OUT,
  output [31:0] bus_OUT
);

  BusRegister busregister_1 (
    .Data_In(data_IN), .Load(Load), .Clock(Clock), .Bus(Bus), .Data_Out(data_OUT), .Bus_Out(bus_OUT));

  // Notes on the sheet:
  //   Isha Mudgal
  //   OLA 5
  //   DR
endmodule

module IR (
  input  [31:0] data_IN,
  input  Clock,
  input  Load,
  output [31:0] data_OUT
);

  Register register_1 (.Data_In(data_IN), .Clock(Clock), .Load(Load), .Data_Out(data_OUT));

  // Notes on the sheet:
  //   Isha Mudgal
  //   OLA 5
  //   IR
endmodule

module OUTR (
  input  [31:0] data_IN,
  input  Clock,
  input  Load,
  output [31:0] data_OUT
);

  Register register_1 (.Data_In(data_IN), .Clock(Clock), .Load(Load), .Data_Out(data_OUT));

  // Notes on the sheet:
  //   Isha Mudgal
  //   OLA 5
  //   OUTregister
endmodule

module PC (
  input  [31:0] data_IN,
  input  Count,
  input  Load,
  input  Clock,
  input  Bus,
  output [31:0] out_6,
  output [31:0] out_7
);

  CountRegister countregister_1 (
    .Data_In(data_IN), .Count(Count), .Load(Load), .Clock(Clock), .Bus(Bus), .Data_Out(out_6), .Bus_Out(out_7));

  // Notes on the sheet:
  //   Isha Mudgal
  //   OLA 5
  //   PC register
endmodule

module R (
  input  [31:0] data_IN,
  input  Load,
  input  Clock,
  input  Bus,
  output [31:0] data_OUT,
  output [31:0] bus_OUT
);

  BusRegister busregister_1 (
    .Data_In(data_IN), .Load(Load), .Clock(Clock), .Bus(Bus), .Data_Out(data_OUT), .Bus_Out(bus_OUT));

  // Notes on the sheet:
  //   Isha Mudgal
  //   OLA 5
  //   R
endmodule
